# Fritzing sketch Ultrasonic Challenge (saved by Fritzing 0.9.3b)
breadboards: 1

parts:
  Part1 = Arduino Uno (Rev3)  # not connected
  Part2 = Arduino Prototyping Shield
  hc-sr1 = hc-sr04
  J2 = Basic Servo
  J3 = Basic Servo
  J4 = Basic Servo
  J1 = Basic Servo

nets:
  N1: Part2.D7, J4.pulse
  VCC: Part2.+5V, hc-sr1.VCC, J2.vcc, J3.vcc, J4.vcc, J1.vcc
  GND: Part2.GND, hc-sr1.GND, J2.gnd, J3.gnd, J4.gnd, J1.gnd
  N2: Part2.D8, Part2.N$281, J3.pulse
  N3: Part2.D9, Part2.N$261, J2.pulse
  N4: Part2.D10, J1.pulse
  N5: Part2.D11, hc-sr1.Trig
  N6: Part2.D12, hc-sr1.Echo
