# Fritzing sketch Midterm Fritzing (saved by Fritzing 0.9.3b)
breadboards: 1

parts:
  hc-sr1 = hc-sr04
  Part1 = Arduino Uno (Rev3)
  J1 = Basic Servo

nets:
  VCC: hc-sr1.VCC, Part1.5V, J1.vcc
  N1: hc-sr1.Trig, Part1.D11_PWM/MOSI
  N2: hc-sr1.Echo, Part1.D12/MISO
  GND: hc-sr1.GND, Part1.GND, J1.gnd
  N3: Part1.D8, J1.pulse
